# Fritzing sketch simple_range_finder (saved by Fritzing 0.9.3b)
breadboards: 1

parts:
  LCD1 = LCD screen
  Part2 = LIDAR-Lite
  C1 = Electrolytic Capacitor [capacitance=100µF package="200 mil [THT, electrolytic]"]
  Part_3 = Arduino Uno (Rev3)
  R2 = Resistor [tolerance=±5% resistance=220 package="0603 [SMD]"]
  1k_Ω = 1k Ω Resistor [package=THT]

nets:
  GND: LCD1.VSS, LCD1.V0, LCD1.R/W, LCD1.LED-, Part2.GND, C1.-, Part_3.GND, 1k_Ω.Pin_1
  5V: LCD1.VDD, Part2.5V, C1.+, Part_3.5V
  N1: LCD1.RS, Part_3.D12/MISO
  N2: LCD1.E, Part_3.D11_PWM/MOSI
  N3: LCD1.DB4, Part_3.D5_PWM
  N4: LCD1.DB5, Part_3.D4
  N5: LCD1.DB6, Part_3.D3_PWM
  N6: LCD1.DB7, 1k_Ω.Pin_0
  N7: LCD1.LED+, Part_3.D2
  N8: Part2.PWR_EN, R2.Pin_1
  N9: Part2.MODE, Part_3.D8
  N10: Part_3.D9_PWM, R2.Pin_0

custom parts:
  LIDAR-Lite: PulsedLight LIDAR-Lite Sensor
  1k Ω Resistor: A generic resistor (0.25W)
